// Logisim project Chenillard JK.circ as structural Verilog: 2 circuits, main circuit main
module main (
  input  in_1
);

  wire chenillard_jk_1_q0, chenillard_jk_1_q1, chenillard_jk_1_q2, clock_1_out;

  Clock clock_1 (.out(clock_1_out));
  Chenillard_JK chenillard_jk_1 (
    .H(clock_1_out), .C(in_1), .Q2(chenillard_jk_1_q2), .Q1(chenillard_jk_1_q1), .Q0(chenillard_jk_1_q0));
  LED S2 (.in(chenillard_jk_1_q2));
  LED S1 (.in(chenillard_jk_1_q1));
  LED S0 (.in(chenillard_jk_1_q0));
endmodule

module Chenillard_JK (
  input  H,
  input  C,
  output Q2,
  output Q1,
  output Q0
);

  wire and_1_out, and_2_out, J0, K0, K1, K2, not_1_out, not_2_out, not_3_out;

  not not_1 (not_1_out, Q2);
  not not_2 (not_2_out, C);
  not not_3 (not_3_out, Q1);
  J_K_Flip_Flop j_k_ff_1 (.J(Q1), .clk(H), .K(K2), .Q(Q2));  // open: Qn, preset, en, reset
  and and_1 (and_1_out, not_3_out, not_1_out);
  and and_2 (and_2_out, Q0, Q1);
  xor xor_1 (K1, Q2, Q1);
  or or_1 (J0, C, and_1_out);
  or or_2 (K2, and_2_out, not_2_out);
  xor xor_2 (K0, Q0, Q1);
  J_K_Flip_Flop j_k_ff_2 (.J(Q0), .clk(H), .K(K1), .Q(Q1));  // open: Qn, preset, en, reset
  J_K_Flip_Flop j_k_ff_3 (.J(J0), .clk(H), .K(K0), .Q(Q0));  // open: Qn, preset, en, reset

  // Other names for the same wires on the sheet: J1 = Q0; J2 = Q1
endmodule
